// Logisim project CSE332_Datapath.circ as structural Verilog: 5 circuits, main circuit main
module main (
  input  in_1,
  input  in_2,
  input  [7:0] in_3
);

  wire and_1_out, Branch, Clk, comparator_1_eq, In_Out, Init, Jump, MemRead, MemtoReg, MemWrite, or_1_out,
       RegWrite, Zero;
  wire [1:0] ALUSrc, RegDest;
  wire [2:0] ALUop, multiplexer_3_out, multiplexer_4_out;
  wire [7:0] adder_1_out, adder_2_out, alu_1_output, bit_extender_3_out, bit_extender_4_out, memory_1_out,
       memory_1_read_data, multiplexer_1_out, multiplexer_2_out, multiplexer_5_out, multiplexer_6_out,
       multiplexer_7_out, multiplexer_8_out, register_1_q, register_2_read_data_1, register_2_read_data_2,
       register_2_t0, register_2_t1;
  wire [8:0] bit_extender_1_out, bit_extender_2_out;
  wire [8:8] adder_2_out_2;
  wire [9:0] rom_1_data;

  Clock clock_1 (.out(Clk));
  Register_part register_1 (.D(multiplexer_1_out), .en(in_1), .Q(register_1_q), .clk(Clk));  // open: clr
  Multiplexer #(.width(8), .enable("false")) multiplexer_1 (
    .in0(adder_1_out), .in1(adder_2_out), .out(multiplexer_1_out), .sel(or_1_out));
  Adder adder_1 (.a(8'h1), .b(register_1_q), .out(adder_1_out));  // open: cin, cout
  or or_1 (or_1_out, and_1_out, Jump);
  ROM #(.dataWidth(10)) rom_1 (.addr(register_1_q), .data(rom_1_data));  // open: sel
  assign bit_extender_1_out = {{1{1'b0}}, adder_1_out};  // Bit_Extender bit_extender_1
  assign bit_extender_2_out = {{3{rom_1_data[5]}}, rom_1_data[5:0]};  // Bit_Extender bit_extender_2
  Adder #(.width(9)) adder_2 (
    .a(bit_extender_1_out), .b(bit_extender_2_out), .out({adder_2_out_2[8], adder_2_out}));  // open: cin, cout
  Multiplexer #(.width(8), .enable("false")) multiplexer_2 (
    .in0(multiplexer_5_out), .in1(bit_extender_3_out), .out(multiplexer_2_out), .sel(Init));
  assign bit_extender_3_out = {{2{rom_1_data[5]}}, rom_1_data[5:0]};  // Bit_Extender bit_extender_3
  Control_Unit control_unit_1 (
    .Opcode(rom_1_data[9:6]), .In_Out(In_Out), .Zero(Zero), .Init(Init), .MemtoReg(MemtoReg),
    .MemRead(MemRead), .MemWrite(MemWrite), .Branch(Branch), .RegDest(RegDest), .Jump(Jump), .ALUop(ALUop),
    .ALUSrc(ALUSrc), .RegWrite(RegWrite));
  and and_1 (and_1_out, comparator_1_eq, Branch);
  Multiplexer #(.width(3), .enable("false")) multiplexer_3 (
    .in0(rom_1_data[5:3]), .in1(3'b000), .out(multiplexer_3_out), .sel(Zero));
  Multiplexer #(.select(2), .width(3), .enable("false")) multiplexer_4 (
    .in0(rom_1_data[5:3]), .in1(3'b100), .in2(3'b101), .out(multiplexer_4_out), .sel(RegDest));  // open: in3
  Comparator comparator_1 (.a({8{1'b0}}), .b(register_2_t1), .eq(comparator_1_eq));  // open: gt, lt
  Register register_2 (
    .Write_Data(multiplexer_2_out), .Read_Register_no_1(multiplexer_3_out), .Write(RegWrite),
    .Write_Register(multiplexer_4_out), .Read_Register_no_2(rom_1_data[2:0]),
    .Read_Data_1(register_2_read_data_1), .Read_Data_2(register_2_read_data_2), .Clock(Clk),
    .T0(register_2_t0), .T1(register_2_t1));
  assign bit_extender_4_out = {{5{1'b0}}, rom_1_data[2:0]};  // Bit_Extender bit_extender_4
  Multiplexer #(.width(8), .enable("false")) multiplexer_5 (
    .in0(alu_1_output), .in1(memory_1_read_data), .out(multiplexer_5_out), .sel(MemtoReg));
  Multiplexer #(.select(2), .width(8), .enable("false")) multiplexer_6 (
    .in0(register_2_read_data_2), .in1(bit_extender_4_out), .in2(register_2_t0), .in3(register_2_t1),
    .out(multiplexer_6_out), .sel(ALUSrc));
  Multiplexer #(.width(8), .enable("false")) multiplexer_7 (
    .in0(register_2_t0), .in1(register_2_read_data_1), .out(multiplexer_7_out), .sel(In_Out));
  Multiplexer #(.width(8), .enable("false")) multiplexer_8 (
    .in0(alu_1_output), .in1(bit_extender_4_out), .out(multiplexer_8_out), .sel(In_Out));
  ALU alu_1 (.Output(alu_1_output), .A(register_2_read_data_1), .B(multiplexer_6_out), .ALUop(ALUop));
  Memory memory_1 (
    .Address(multiplexer_8_out), .In(in_3), .Write_Data(multiplexer_7_out), .MemWrite(MemWrite),
    .MemRead(MemRead), .Clock(Clk), .Out(memory_1_out), .Read_Data(memory_1_read_data), .InStr(in_2));
  Hex_Digit_Display hex_digit_display_1 (.value(memory_1_out[7:4]));  // open: dp
  Hex_Digit_Display hex_digit_display_2 (.value(memory_1_out[3:0]));  // open: dp

  // Notes on the sheet:
  //   contents of rom_1 (hex, n*v repeats v):
  //   2c2 30c 2c1 314 2c4 31c 251 334 3b1 249 33c 3b9 32f 2e 3a9 325 28b
  //   INPUT
  //   OUTPUT
endmodule

module Register (
  input  [7:0] Write_Data,
  input  Clock,
  input  [2:0] Read_Register_no_1,
  input  Write,
  input  [2:0] Write_Register,
  input  [2:0] Read_Register_no_2,
  output [7:0] Read_Data_1,
  output [7:0] T0,
  output [7:0] T1,
  output [7:0] Read_Data_2
);

  wire e1, e2, e3, e4, e5, e6, e7, e8;
  wire [7:0] r2, r3, r4, r7, r8;

  Decoder #(.select(3), .disabled(0)) decoder_1 (
    .out0(e1), .out1(e2), .out2(e3), .out3(e4), .out4(e5), .out5(e6), .out6(e7), .out7(e8),
    .sel(Write_Register), .en(Write));
  Register_part register_1 (.D(Write_Data), .en(e2), .Q(r2), .clk(Clock));  // open: clr
  Register_part register_2 (.D(Write_Data), .en(e3), .Q(r3), .clk(Clock));  // open: clr
  Register_part register_3 (.D(Write_Data), .en(e4), .Q(r4), .clk(Clock));  // open: clr
  Register_part register_4 (.D(Write_Data), .en(e5), .Q(T0), .clk(Clock));  // open: clr
  Register_part register_5 (.D(Write_Data), .en(e6), .Q(T1), .clk(Clock));  // open: clr
  Register_part register_6 (.D(Write_Data), .en(e7), .Q(r7), .clk(Clock));  // open: clr
  Register_part register_7 (.D(Write_Data), .en(e8), .Q(r8), .clk(Clock));  // open: clr
  Multiplexer #(.select(3), .width(8), .disabled(0), .enable("false")) multiplexer_1 (
    .in0({8{1'b0}}), .in1(r2), .in2(r3), .in3(r4), .in4(T0), .in5(T1), .in6(r7), .in7(r8), .out(Read_Data_1),
    .sel(Read_Register_no_1));
  Multiplexer #(.select(3), .width(8), .disabled(0), .enable("false")) multiplexer_2 (
    .in0({8{1'b0}}), .in1(r2), .in2(r3), .in3(r4), .in4(T0), .in5(T1), .in6(r7), .in7(r8), .out(Read_Data_2),
    .sel(Read_Register_no_2));

  // Other names for the same wires on the sheet: r5[7:0] = T0; r6[7:0] = T1

  // Notes on the sheet:
  //   $Zero
  //   $S0
  //   $S1
  //   $S2
  //   $T0
  //   $T1
  //   $T2
  //   $T3
endmodule

module ALU (
  input  [7:0] A,
  input  [7:0] B,
  input  [2:0] ALUop,
  output [7:0] Output
);

  wire comparator_1_eq, comparator_1_lt;
  wire [2:0] bit_extender_1_out, bit_extender_2_out;
  wire [7:0] adder_1_out, bit_extender_3_out, bit_extender_4_out, nand_1_out, shifter_1_out, shifter_2_out,
       subtractor_1_out;

  Bit_Extender #(.out_width(3)) bit_extender_1 (.in(B), .out(bit_extender_1_out));
  Bit_Extender #(.out_width(3)) bit_extender_2 (.in(B), .out(bit_extender_2_out));
  Adder adder_1 (.a(A), .b(B), .out(adder_1_out));  // open: cin, cout
  Subtractor subtractor_1 (.a(A), .b(B), .out(subtractor_1_out));  // open: bin, bout
  assign nand_1_out = ~(A & B);  // NAND_Gate nand_1, 8 bits wide
  Shifter shifter_1 (.in(A), .\dist (bit_extender_1_out), .out(shifter_1_out));
  Shifter #(.shift("lr")) shifter_2 (.in(A), .\dist (bit_extender_2_out), .out(shifter_2_out));
  Comparator comparator_1 (.a(A), .b(B), .eq(comparator_1_eq), .lt(comparator_1_lt));  // open: gt
  assign bit_extender_3_out = {{7{1'b0}}, comparator_1_eq};  // Bit_Extender bit_extender_3
  assign bit_extender_4_out = {{7{1'b0}}, comparator_1_lt};  // Bit_Extender bit_extender_4
  Multiplexer #(.select(3), .width(8), .enable("false")) multiplexer_1 (
    .in0(adder_1_out), .in1(subtractor_1_out), .in2(nand_1_out), .in3(shifter_1_out), .in4(shifter_2_out),
    .in5(bit_extender_3_out), .in6(bit_extender_4_out), .out(Output), .sel(ALUop));  // open: in7
endmodule

module Memory (
  input  [7:0] Address,
  input  [7:0] In,
  input  InStr,
  input  [7:0] Write_Data,
  input  MemWrite,
  input  MemRead,
  input  Clock,
  output [7:0] Out,
  output [7:0] Read_Data
);

  wire and_1_out, comparator_1_eq, comparator_2_eq, or_1_out;
  wire [7:0] multiplexer_1_out, ram_1_data, register_1_q;

  and and_1 (and_1_out, comparator_2_eq, MemWrite);
  Comparator comparator_1 (.a(Address), .b({8{1'b0}}), .eq(comparator_1_eq));  // open: gt, lt
  Comparator comparator_2 (.a(Address), .b(8'h1), .eq(comparator_2_eq));  // open: gt, lt
  or or_1 (or_1_out, comparator_1_eq, comparator_2_eq);
  Register_part register_1 (.D(In), .en(InStr), .Q(register_1_q), .clk(Clock));  // open: clr
  Multiplexer #(.width(8)) multiplexer_1 (
    .in0(register_1_q), .in1(Out), .out(multiplexer_1_out), .sel(Address[0]), .en(MemRead));
  Register_part register_2 (.D(Write_Data), .en(and_1_out), .Q(Out), .clk(Clock));  // open: clr
  RAM #(.bus("separate")) ram_1 (
    .addr(Address), .din(Write_Data), .data(ram_1_data), .str(MemWrite), .clk(Clock), .ld(MemRead));  // open: sel, clr
  Multiplexer #(.width(8), .enable("false")) multiplexer_2 (
    .in0(ram_1_data), .in1(multiplexer_1_out), .out(Read_Data), .sel(or_1_out));
endmodule

module Control_Unit (
  input  [3:0] Opcode,
  output In_Out,
  output Zero,
  output Init,
  output MemtoReg,
  output MemRead,
  output MemWrite,
  output Branch,
  output [1:0] RegDest,
  output Jump,
  output [2:0] ALUop,
  output [1:0] ALUSrc,
  output RegWrite
);

  Multiplexer #(.select(4), .width(16), .enable("false")) multiplexer_1 (
    .in0(16'h8000), .in1(16'h8400), .in2(16'h8800), .in3(16'hac00), .in4(16'hb000), .in5(16'h200),
    .in6(16'h40), .in7(16'h9500), .in8(16'h9900), .in9(16'h8098), .in10(16'h20), .in11(16'h8084),
    .in12(16'h8002), .in13(16'h8019), .in14(16'h21),
    .out({RegWrite, ALUSrc, ALUop, Jump, RegDest, Branch, MemWrite, MemRead, MemtoReg, Init, Zero, In_Out}),
    .sel(Opcode));  // open: in15
endmodule
